// Logisim project path.circ as structural Verilog: 9 circuits, main circuit Path
module main (
  input  [4:0] in_1,
  input  [31:0] in_2,
  input  [31:0] in_3,
  output out_4,
  output [31:0] out_5
);

  wire comparator_1_lt, comparator_2_lt, comparator_3_eq, comparator_4_eq, comparator_4_gt, comparator_4_lt,
       comparator_5_eq, comparator_6_eq, not_1_out, or_2_out;
  wire [31:0] adder_1_out, and_1_out, multiplexer_1_out, multiplexer_2_out, multiplexer_3_out,
       multiplexer_4_out, multiplexer_5_out, multiplexer_6_out, or_1_out, shifter_1_out, shifter_2_out,
       shifter_3_out, subtractor_1_out, xor_1_out;

  assign and_1_out = in_2 & in_3;  // AND_Gate and_1, 32 bits wide
  Adder #(.width(32)) adder_1 (.a(in_2), .b(in_3), .out(adder_1_out));  // open: cin, cout
  Comparator #(.width(32), .mode("unsigned")) comparator_1 (.a(in_2), .b(in_3), .lt(comparator_1_lt));  // open: gt, eq
  Subtractor #(.width(32)) subtractor_1 (.a(in_2), .b(in_3), .out(subtractor_1_out));  // open: bin, bout
  Shifter #(.width(32), .shift("lr")) shifter_1 (.in(in_2), .\dist (in_3[4:0]), .out(shifter_1_out));
  Shifter #(.width(32), .shift("ar")) shifter_2 (.in(in_2), .\dist (in_3[4:0]), .out(shifter_2_out));
  Shifter #(.width(32)) shifter_3 (.in(in_2), .\dist (in_3[4:0]), .out(shifter_3_out));
  assign xor_1_out = in_2 ^ in_3;  // XOR_Gate xor_1, 32 bits wide
  Comparator #(.width(32)) comparator_2 (.a(in_2), .b(in_3), .lt(comparator_2_lt));  // open: gt, eq
  Comparator #(.width(32)) comparator_3 (.a(in_2), .b(in_3), .eq(comparator_3_eq));  // open: gt, lt
  Comparator #(.width(32)) comparator_4 (
    .a(in_2), .b(in_3), .gt(comparator_4_gt), .eq(comparator_4_eq), .lt(comparator_4_lt));
  assign or_1_out = in_2 | in_3;  // OR_Gate or_1, 32 bits wide
  Multiplexer #(.width(32), .disabled(0), .enable("false")) multiplexer_1 (
    .in0({32{1'b0}}), .in1(32'h1), .out(multiplexer_1_out), .sel(comparator_1_lt));
  or or_2 (or_2_out, comparator_4_gt, comparator_4_eq);
  Multiplexer #(.width(32), .disabled(0), .enable("false")) multiplexer_2 (
    .in0({32{1'b0}}), .in1(32'h1), .out(multiplexer_2_out), .sel(comparator_2_lt));
  Multiplexer #(.width(32), .disabled(0), .enable("false")) multiplexer_3 (
    .in0({32{1'b0}}), .in1(32'h1), .out(multiplexer_3_out), .sel(comparator_3_eq));
  Multiplexer #(.width(32), .disabled(0), .enable("false")) multiplexer_4 (
    .in0({32{1'b0}}), .in1(32'h1), .out(multiplexer_4_out), .sel(or_2_out));
  Multiplexer #(.width(32), .disabled(0), .enable("false")) multiplexer_5 (
    .in0({32{1'b0}}), .in1(32'h1), .out(multiplexer_5_out), .sel(comparator_4_lt));
  Multiplexer #(.width(32), .disabled(0), .enable("false")) multiplexer_6 (
    .in0({32{1'b0}}), .in1(32'h1), .out(multiplexer_6_out), .sel(not_1_out));
  not not_1 (not_1_out, comparator_4_eq);
  Multiplexer #(.select(5), .width(32), .disabled(0), .enable("false")) multiplexer_7 (
    .in0(adder_1_out), .in1(shifter_3_out), .in2(multiplexer_2_out), .in3(multiplexer_1_out),
    .in4(xor_1_out), .in5(shifter_1_out), .in6(or_1_out), .in7(and_1_out), .in8(subtractor_1_out),
    .in13(shifter_2_out), .in16(multiplexer_3_out), .in17(multiplexer_6_out), .in20(multiplexer_5_out),
    .in21(multiplexer_4_out), .out(out_5), .sel(in_1));  // open: in9, in10, in11, in12, in14, in15, in18, in19, in22, in23, in24, in25, in26, in27, in28, in29, in30, in31
  Comparator #(.width(2)) comparator_5 (.a(in_1[4:3]), .b(2'b10), .eq(comparator_5_eq));  // open: gt, lt
  Comparator #(.width(32)) comparator_6 (.a(32'h1), .b(out_5), .eq(comparator_6_eq));  // open: gt, lt
  and and_2 (out_4, comparator_5_eq, comparator_6_eq);

  // Notes on the sheet:
  //   A
  //   B
  //   Branch
endmodule

module regF (
  input  [31:0] in_1,
  input  Wen,
  input  [4:0] RS1,
  input  [4:0] RD,
  input  [4:0] RS2,
  input  in_6,
  input  in_7,
  output [31:0] out_8,
  output [31:0] out_9
);

  wire decoder_1_out0, decoder_1_out1, decoder_1_out2, decoder_1_out3, decoder_1_out4, decoder_1_out5,
       decoder_1_out6, decoder_1_out7, decoder_1_out8, decoder_1_out9, decoder_1_out10, decoder_1_out11,
       decoder_1_out12, decoder_1_out13, decoder_1_out14, decoder_1_out15, decoder_1_out16, decoder_1_out17,
       decoder_1_out18, decoder_1_out19, decoder_1_out20, decoder_1_out21, decoder_1_out22, decoder_1_out23,
       decoder_1_out24, decoder_1_out25, decoder_1_out26, decoder_1_out27, decoder_1_out28, decoder_1_out29,
       decoder_1_out30, decoder_1_out31;
  wire [31:0] multiplexer_1_out, register_1_q, register_2_q, register_3_q, register_4_q, register_5_q,
       register_6_q, register_7_q, register_8_q, register_9_q, register_10_q, register_11_q, register_12_q,
       register_13_q, register_14_q, register_15_q, register_16_q, register_17_q, register_18_q,
       register_19_q, register_20_q, register_21_q, register_22_q, register_23_q, register_24_q,
       register_25_q, register_26_q, register_27_q, register_28_q, register_29_q, register_30_q,
       register_31_q, register_32_q;

  Decoder #(.select(5)) decoder_1 (
    .out0(decoder_1_out0), .out1(decoder_1_out1), .out2(decoder_1_out2), .out3(decoder_1_out3),
    .out4(decoder_1_out4), .out5(decoder_1_out5), .out6(decoder_1_out6), .out7(decoder_1_out7),
    .out8(decoder_1_out8), .out9(decoder_1_out9), .out10(decoder_1_out10), .out11(decoder_1_out11),
    .out12(decoder_1_out12), .out13(decoder_1_out13), .out14(decoder_1_out14), .out15(decoder_1_out15),
    .out16(decoder_1_out16), .out17(decoder_1_out17), .out18(decoder_1_out18), .out19(decoder_1_out19),
    .out20(decoder_1_out20), .out21(decoder_1_out21), .out22(decoder_1_out22), .out23(decoder_1_out23),
    .out24(decoder_1_out24), .out25(decoder_1_out25), .out26(decoder_1_out26), .out27(decoder_1_out27),
    .out28(decoder_1_out28), .out29(decoder_1_out29), .out30(decoder_1_out30), .out31(decoder_1_out31),
    .sel(RD), .en(Wen));
  Multiplexer #(.width(32)) multiplexer_1 (.in1(in_1), .out(multiplexer_1_out), .sel(Wen));  // open: in0, en
  Register #(.width(32)) register_1 (.D({32{1'b0}}), .en(decoder_1_out0), .Q(register_1_q), .clk(in_6), .clr(in_7));
  Register #(.width(32)) register_2 (
    .D(multiplexer_1_out), .en(decoder_1_out1), .Q(register_2_q), .clk(in_6), .clr(in_7));
  Register #(.width(32)) register_3 (
    .D(multiplexer_1_out), .en(decoder_1_out2), .Q(register_3_q), .clk(in_6), .clr(in_7));
  Register #(.width(32)) register_4 (
    .D(multiplexer_1_out), .en(decoder_1_out3), .Q(register_4_q), .clk(in_6), .clr(in_7));
  Register #(.width(32)) register_5 (
    .D(multiplexer_1_out), .en(decoder_1_out4), .Q(register_5_q), .clk(in_6), .clr(in_7));
  Register #(.width(32)) register_6 (
    .D(multiplexer_1_out), .en(decoder_1_out5), .Q(register_6_q), .clk(in_6), .clr(in_7));
  Register #(.width(32)) register_7 (
    .D(multiplexer_1_out), .en(decoder_1_out6), .Q(register_7_q), .clk(in_6), .clr(in_7));
  Register #(.width(32)) register_8 (
    .D(multiplexer_1_out), .en(decoder_1_out7), .Q(register_8_q), .clk(in_6), .clr(in_7));
  Register #(.width(32)) register_9 (
    .D(multiplexer_1_out), .en(decoder_1_out8), .Q(register_9_q), .clk(in_6), .clr(in_7));
  Register #(.width(32)) register_10 (
    .D(multiplexer_1_out), .en(decoder_1_out9), .Q(register_10_q), .clk(in_6), .clr(in_7));
  Register #(.width(32)) register_11 (
    .D(multiplexer_1_out), .en(decoder_1_out10), .Q(register_11_q), .clk(in_6), .clr(in_7));
  Register #(.width(32)) register_12 (
    .D(multiplexer_1_out), .en(decoder_1_out11), .Q(register_12_q), .clk(in_6), .clr(in_7));
  Register #(.width(32)) register_13 (
    .D(multiplexer_1_out), .en(decoder_1_out12), .Q(register_13_q), .clk(in_6), .clr(in_7));
  Register #(.width(32)) register_14 (
    .D(multiplexer_1_out), .en(decoder_1_out13), .Q(register_14_q), .clk(in_6), .clr(in_7));
  Register #(.width(32)) register_15 (
    .D(multiplexer_1_out), .en(decoder_1_out14), .Q(register_15_q), .clk(in_6), .clr(in_7));
  Register #(.width(32)) register_16 (
    .D(multiplexer_1_out), .en(decoder_1_out15), .Q(register_16_q), .clk(in_6), .clr(in_7));
  Register #(.width(32)) register_17 (
    .D(multiplexer_1_out), .en(decoder_1_out16), .Q(register_17_q), .clk(in_6), .clr(in_7));
  Register #(.width(32)) register_18 (
    .D(multiplexer_1_out), .en(decoder_1_out17), .Q(register_18_q), .clk(in_6), .clr(in_7));
  Register #(.width(32)) register_19 (
    .D(multiplexer_1_out), .en(decoder_1_out18), .Q(register_19_q), .clk(in_6), .clr(in_7));
  Register #(.width(32)) register_20 (
    .D(multiplexer_1_out), .en(decoder_1_out19), .Q(register_20_q), .clk(in_6), .clr(in_7));
  Register #(.width(32)) register_21 (
    .D(multiplexer_1_out), .en(decoder_1_out20), .Q(register_21_q), .clk(in_6), .clr(in_7));
  Register #(.width(32)) register_22 (
    .D(multiplexer_1_out), .en(decoder_1_out21), .Q(register_22_q), .clk(in_6), .clr(in_7));
  Register #(.width(32)) register_23 (
    .D(multiplexer_1_out), .en(decoder_1_out22), .Q(register_23_q), .clk(in_6), .clr(in_7));
  Register #(.width(32)) register_24 (
    .D(multiplexer_1_out), .en(decoder_1_out23), .Q(register_24_q), .clk(in_6), .clr(in_7));
  Register #(.width(32)) register_25 (
    .D(multiplexer_1_out), .en(decoder_1_out24), .Q(register_25_q), .clk(in_6), .clr(in_7));
  Register #(.width(32)) register_26 (
    .D(multiplexer_1_out), .en(decoder_1_out25), .Q(register_26_q), .clk(in_6), .clr(in_7));
  Register #(.width(32)) register_27 (
    .D(multiplexer_1_out), .en(decoder_1_out26), .Q(register_27_q), .clk(in_6), .clr(in_7));
  Register #(.width(32)) register_28 (
    .D(multiplexer_1_out), .en(decoder_1_out27), .Q(register_28_q), .clk(in_6), .clr(in_7));
  Register #(.width(32)) register_29 (
    .D(multiplexer_1_out), .en(decoder_1_out28), .Q(register_29_q), .clk(in_6), .clr(in_7));
  Register #(.width(32)) register_30 (
    .D(multiplexer_1_out), .en(decoder_1_out29), .Q(register_30_q), .clk(in_6), .clr(in_7));
  Register #(.width(32)) register_31 (
    .D(multiplexer_1_out), .en(decoder_1_out30), .Q(register_31_q), .clk(in_6), .clr(in_7));
  Register #(.width(32)) register_32 (
    .D(multiplexer_1_out), .en(decoder_1_out31), .Q(register_32_q), .clk(in_6), .clr(in_7));
  Multiplexer #(.select(5), .width(32), .enable("false")) multiplexer_2 (
    .in0(register_1_q), .in1(register_2_q), .in2(register_3_q), .in3(register_4_q), .in4(register_5_q),
    .in5(register_6_q), .in6(register_7_q), .in7(register_8_q), .in8(register_9_q), .in9(register_10_q),
    .in10(register_11_q), .in11(register_12_q), .in12(register_13_q), .in13(register_14_q),
    .in14(register_15_q), .in15(register_16_q), .in16(register_17_q), .in17(register_18_q),
    .in18(register_19_q), .in19(register_20_q), .in20(register_21_q), .in21(register_22_q),
    .in22(register_23_q), .in23(register_24_q), .in24(register_25_q), .in25(register_26_q),
    .in26(register_27_q), .in27(register_28_q), .in28(register_29_q), .in29(register_30_q),
    .in30(register_31_q), .in31(register_32_q), .out(out_8), .sel(RS1));
  Multiplexer #(.select(5), .width(32), .enable("false")) multiplexer_3 (
    .in0(register_1_q), .in1(register_2_q), .in2(register_3_q), .in3(register_4_q), .in4(register_5_q),
    .in5(register_6_q), .in6(register_7_q), .in7(register_8_q), .in8(register_9_q), .in9(register_10_q),
    .in10(register_11_q), .in11(register_12_q), .in12(register_13_q), .in13(register_14_q),
    .in14(register_15_q), .in15(register_16_q), .in16(register_17_q), .in17(register_18_q),
    .in18(register_19_q), .in19(register_20_q), .in20(register_21_q), .in21(register_22_q),
    .in22(register_23_q), .in23(register_24_q), .in24(register_25_q), .in25(register_26_q),
    .in26(register_27_q), .in27(register_28_q), .in28(register_29_q), .in29(register_30_q),
    .in30(register_31_q), .in31(register_32_q), .out(out_9), .sel(RS2));
endmodule

module Path (
  output [4:0] out_1
);

  wire adder_1_cout, and_1_out, button_1_out, clock_1_out, cu_1_out_2, cu_1_out_3, cu_1_out_5, cu_1_out_6,
       cu_1_out_7, cu_1_out_9, cu_1_out_10, main_1_out_4, or_1_out, or_2_out;
  wire [1:0] cu_1_out_4;
  wire [4:0] multiplexer_5_out, multiplexer_10_out;
  wire [6:0] rom_1_data;
  wire [31:0] adder_1_out, imm_gen_1_i_type_imme, imm_gen_1_s_b_type_imme, imm_gen_1_s_type_imme,
       imm_gen_1_u_type, imm_gen_1_uj_type, main_1_out_5, multiplexer_1_out, multiplexer_2_out,
       multiplexer_3_out, multiplexer_4_out, multiplexer_6_out, multiplexer_7_out, multiplexer_8_out,
       multiplexer_9_out, multiplexer_11_out, ram_1_data, regf_1_out_8, regf_1_out_9, register_1_q;
  wire [31:7] rom_1_data_2;

  Multiplexer #(.width(32), .enable("false")) multiplexer_1 (
    .in0(adder_1_out), .in1(imm_gen_1_s_b_type_imme), .out(multiplexer_1_out), .sel(and_1_out));
  Multiplexer #(.width(32), .enable("false")) multiplexer_2 (
    .in0(multiplexer_1_out), .in1(imm_gen_1_uj_type), .out(multiplexer_2_out), .sel(cu_1_out_10));
  Register #(.width(32)) register_1 (
    .D(multiplexer_3_out), .Q(register_1_q), .clk(clock_1_out), .clr(button_1_out));  // open: en
  Button button_1 (.out(button_1_out));
  Multiplexer #(.width(32), .enable("false")) multiplexer_3 (
    .in0(multiplexer_2_out), .in1(main_1_out_5), .out(multiplexer_3_out), .sel(cu_1_out_9));
  // Probe on adder_1_out
  Clock clock_1 (.out(clock_1_out));
  Adder #(.width(32)) adder_1 (.a(32'h4), .b(register_1_q), .out(adder_1_out), .cout(adder_1_cout));  // open: cin
  and and_1 (and_1_out, main_1_out_4, cu_1_out_2);
  ROM #(.addrWidth(24), .dataWidth(32)) rom_1 (
    .addr(register_1_q[25:2]), .data({rom_1_data_2, rom_1_data}));  // open: sel
  // Probe on imm_gen_1_uj_type
  CU cu_1 (
    .in_1(rom_1_data), .out_2(cu_1_out_2), .out_3(cu_1_out_3), .out_4(cu_1_out_4[0]), .out_5(cu_1_out_5),
    .out_6(cu_1_out_6), .out_7(cu_1_out_7), .out_8(cu_1_out_4[1]), .out_9(cu_1_out_9), .out_10(cu_1_out_10));
  Multiplexer #(.width(32), .enable("false")) multiplexer_4 (
    .in0(multiplexer_6_out), .in1(adder_1_out), .out(multiplexer_4_out), .sel(cu_1_out_10));
  Multiplexer #(.width(5), .enable("false")) multiplexer_5 (
    .in0(rom_1_data_2[11:7]), .in1(5'b00001), .out(multiplexer_5_out), .sel(cu_1_out_10));
  // Probe on multiplexer_5_out
  // Probe on rom_1_data_2[19:15]
  // Probe on rom_1_data_2[24:20]
  Imm_Gen imm_gen_1 (
    .in_1({rom_1_data_2, rom_1_data}), .I_type_imme(imm_gen_1_i_type_imme), .in_2(register_1_q),
    .S_type_Imme(imm_gen_1_s_type_imme), .S_B_type_Imme(imm_gen_1_s_b_type_imme), .U_Type(imm_gen_1_u_type),
    .UJ_Type(imm_gen_1_uj_type));
  Multiplexer #(.width(32)) multiplexer_6 (
    .in0(multiplexer_11_out), .in1(imm_gen_1_u_type), .out(multiplexer_6_out), .sel(cu_1_out_7));  // open: en
  Multiplexer #(.width(32), .enable("false")) multiplexer_7 (
    .in0(regf_1_out_8), .in1(adder_1_out), .out(multiplexer_7_out), .sel(cu_1_out_4[1]));
  regF regf_1 (
    .in_1(multiplexer_4_out), .RS1(rom_1_data_2[19:15]), .Wen(cu_1_out_3), .RD(multiplexer_5_out),
    .RS2(rom_1_data_2[24:20]), .in_7(button_1_out), .out_8(regf_1_out_8), .out_9(regf_1_out_9),
    .in_6(clock_1_out));
  Multiplexer #(.select(2), .width(32), .enable("false")) multiplexer_8 (
    .in0(regf_1_out_9), .in1(multiplexer_9_out), .in2(imm_gen_1_u_type), .out(multiplexer_8_out),
    .sel(cu_1_out_4));  // open: in3
  Multiplexer #(.width(32), .enable("false")) multiplexer_9 (
    .in0(imm_gen_1_i_type_imme), .in1(imm_gen_1_s_type_imme), .out(multiplexer_9_out), .sel(or_2_out));
  \function  function_1 (.out_4(out_1), .in_1(rom_1_data_2[30]), .in_2(rom_1_data_2[14:12]), .in_3(cu_1_out_2));
  or or_1 (or_1_out, cu_1_out_6, cu_1_out_5);
  // Probe on multiplexer_10_out
  Multiplexer #(.width(5), .enable("false")) multiplexer_10 (
    .in0(out_1), .in1({5{1'b0}}), .out(multiplexer_10_out), .sel(or_1_out));
  or or_2 (or_2_out, cu_1_out_6, cu_1_out_5);
  main main_1 (
    .in_2(multiplexer_7_out), .in_3(multiplexer_8_out), .in_1(multiplexer_10_out), .out_4(main_1_out_4),
    .out_5(main_1_out_5));
  RAM #(.addrWidth(24), .dataWidth(32), .bus("separate")) ram_1 (
    .addr(main_1_out_5[23:0]), .din(regf_1_out_9), .data(ram_1_data), .str(cu_1_out_6), .clk(clock_1_out),
    .ld(cu_1_out_5), .clr(button_1_out));  // open: sel
  // Probe on regf_1_out_9
  Multiplexer #(.width(32)) multiplexer_11 (
    .in0(main_1_out_5), .in1(ram_1_data), .out(multiplexer_11_out), .sel(cu_1_out_5));  // open: en

  // Notes on the sheet:
  //   contents of rom_1 (hex, n*v repeats v):
  //   800113 202423 802183
endmodule

module Imm_Gen (
  input  [31:0] in_1,
  input  [31:0] in_2,
  output [31:0] I_type_imme,
  output [31:0] S_type_Imme,
  output [31:0] S_B_type_Imme,
  output [31:0] U_Type,
  output [31:0] UJ_Type
);

  wire [31:0] bit_extender_2_out, bit_extender_3_out, bit_extender_5_out;

  assign S_type_Imme = {{20{in_1[31]}}, {in_1[31:25], in_1[11:7]}};  // Bit_Extender bit_extender_1
  assign bit_extender_2_out = {{19{in_1[31]}}, {in_1[31], in_1[7], in_1[30:25], in_1[11:8], 1'b0}};  // Bit_Extender bit_extender_2
  assign bit_extender_3_out = {{12{in_1[31]}}, in_1[31:12]};  // Bit_Extender bit_extender_3
  assign I_type_imme = {{20{in_1[31]}}, in_1[31:20]};  // Bit_Extender bit_extender_4
  assign bit_extender_5_out = {{11{in_1[31]}}, {in_1[31], in_1[19:12], in_1[20], in_1[30:21], 1'b0}};  // Bit_Extender bit_extender_5
  Adder #(.width(32)) adder_1 (.a(in_2), .b(bit_extender_2_out), .out(S_B_type_Imme));  // open: cin, cout
  Shifter #(.width(32)) shifter_1 (.in(bit_extender_3_out), .\dist (5'b01100), .out(U_Type));
  Adder #(.width(32)) adder_2 (.a(in_2), .b(bit_extender_5_out), .out(UJ_Type));  // open: cin, cout

  // Notes on the sheet:
  //   instruction
  //   PC
endmodule

module Opc_Decoder (
  input  [6:0] OpCode,
  output R_Type,
  output I_Type,
  output B_Type,
  output L_Type,
  output S_Type,
  output U_Type,
  output UJ_Type,
  output auipc,
  output auipc_2
);

  Comparator #(.width(7)) comparator_1 (.a(7'b0110011), .b(OpCode), .eq(R_Type));  // open: gt, lt
  Comparator #(.width(7)) comparator_2 (.a(7'b0010011), .b(OpCode), .eq(I_Type));  // open: gt, lt
  Comparator #(.width(7)) comparator_3 (.a(7'b1100011), .b(OpCode), .eq(B_Type));  // open: gt, lt
  Comparator #(.width(7)) comparator_4 (.a(7'b0000011), .b(OpCode), .eq(L_Type));  // open: gt, lt
  Comparator #(.width(7)) comparator_5 (.a(7'b0100011), .b(OpCode), .eq(S_Type));  // open: gt, lt
  Comparator #(.width(7)) comparator_6 (.a(7'b0110111), .b(OpCode), .eq(U_Type));  // open: gt, lt
  Comparator #(.width(7)) comparator_7 (.a(7'b1101111), .b(OpCode), .eq(UJ_Type));  // open: gt, lt
  Comparator #(.width(7)) comparator_8 (.a(7'b0010111), .b(OpCode), .eq(auipc));  // open: gt, lt
  Comparator #(.width(7)) comparator_9 (.a(7'b1100111), .b(OpCode), .eq(auipc_2));  // open: gt, lt
endmodule

module Cntrl (
  input  L_Type,
  input  S_Type,
  input  R_Type,
  input  l_Type_2,
  input  B_Type,
  input  U_Type,
  input  auipc,
  input  jalr,
  input  UJ,
  output Branch,
  output RegWrite,
  output operand_B_sel,
  output Store,
  output Load,
  output U,
  output out_16,
  output jalr_2,
  output jal
);

  or or_1 (RegWrite, UJ, U_Type, R_Type, l_Type_2, L_Type, auipc);
  or or_2 (operand_B_sel, l_Type_2, S_Type, L_Type);

  assign Branch = B_Type;
  assign jal = UJ;
  assign jalr_2 = jalr;
  assign Load = L_Type;
  assign out_16 = auipc;
  assign Store = S_Type;
  assign U = U_Type;
endmodule

module CU (
  input  [6:0] in_1,
  output out_2,
  output out_3,
  output out_4,
  output out_5,
  output out_6,
  output out_7,
  output out_8,
  output out_9,
  output out_10
);

  wire opc_decoder_1_auipc, opc_decoder_1_auipc_2, opc_decoder_1_b_type, opc_decoder_1_i_type,
       opc_decoder_1_l_type, opc_decoder_1_r_type, opc_decoder_1_s_type, opc_decoder_1_u_type,
       opc_decoder_1_uj_type;

  Opc_Decoder opc_decoder_1 (
    .OpCode(in_1), .R_Type(opc_decoder_1_r_type), .I_Type(opc_decoder_1_i_type),
    .B_Type(opc_decoder_1_b_type), .L_Type(opc_decoder_1_l_type), .S_Type(opc_decoder_1_s_type),
    .U_Type(opc_decoder_1_u_type), .UJ_Type(opc_decoder_1_uj_type), .auipc(opc_decoder_1_auipc),
    .auipc_2(opc_decoder_1_auipc_2));
  Cntrl cntrl_1 (
    .Branch(out_2), .RegWrite(out_3), .operand_B_sel(out_4), .Store(out_6), .Load(out_5),
    .L_Type(opc_decoder_1_l_type), .S_Type(opc_decoder_1_s_type), .R_Type(opc_decoder_1_r_type),
    .l_Type_2(opc_decoder_1_i_type), .B_Type(opc_decoder_1_b_type), .U_Type(opc_decoder_1_u_type), .U(out_7),
    .auipc(opc_decoder_1_auipc), .out_16(out_8), .jalr(opc_decoder_1_auipc_2), .jalr_2(out_9),
    .UJ(opc_decoder_1_uj_type), .jal(out_10));
endmodule

module Alucntrl (
  input  [31:0] in_1,
  input  in_2,
  output [4:0] out_3
);

  Multiplexer #(.width(5), .enable("false")) multiplexer_1 (
    .in0({1'b0, in_1[30], in_1[14:12]}), .in1({2'b10, in_1[14:12]}), .out(out_3), .sel(in_2));
endmodule

module \function  (
  input  in_1,
  input  [2:0] in_2,
  input  in_3,
  output [4:0] out_4
);

  Multiplexer #(.width(5)) multiplexer_1 (
    .in0({1'b0, in_1, in_2}), .in1({2'b10, in_2}), .out(out_4), .sel(in_3));  // open: en
endmodule
